// Logisim project main.circ as structural Verilog
module main (
  input  in_1
);

  wire and_1_out, and_2_out, and_3_out, clock_1_out, multiplexer_2_out, not_1_out, not_2_out, not_3_out,
       not_4_out, not_5_out, or_1_out;
  wire [1:0] controlled_buffer_1_out;
  wire [3:0] controlled_buffer_1_out_3, controlled_buffer_6_out_2, multiplexer_1_out;
  wire [7:0] adder_1_out, controlled_buffer_5_out, register_1_q;
  wire [15:0] alu_1_output, controlled_buffer_2_out, controlled_buffer_4_out, controlled_buffer_5_out_2,
       controlled_buffer_6_out, demultiplexer_1_out0, demultiplexer_1_out1, demultiplexer_2_out0,
       demultiplexer_2_out1, demultiplexer_3_out0, demultiplexer_3_out1, multiplexer_3_out, ram_1_data,
       registerfile_1_readdata_1, registerfile_1_readdata_2, rom_1_data;
  wire [15:2] controlled_buffer_1_out_2;

  Register register_1 (.D(adder_1_out), .Q(register_1_q), .clk(clock_1_out));  // open: en, clr
  Adder adder_1 (.a(register_1_q), .b(8'h1), .out(adder_1_out));  // open: cin, cout
  Clock clock_1 (.out(clock_1_out));
  ROM #(.dataWidth(16)) rom_1 (.addr(register_1_q), .data(rom_1_data));  // open: sel
  Demultiplexer #(.width(16), .enable("false")) demultiplexer_1 (
    .out0(demultiplexer_1_out0), .out1(demultiplexer_1_out1), .in(rom_1_data), .sel(rom_1_data[15]));
  assign {controlled_buffer_1_out_2[15], controlled_buffer_1_out_3, controlled_buffer_1_out_2[10:2], controlled_buffer_1_out} = not_1_out ? demultiplexer_1_out0 : 16'bz;  // Controlled_Buffer controlled_buffer_1
  not not_1 (not_1_out, rom_1_data[15]);
  assign controlled_buffer_2_out = rom_1_data[15] ? demultiplexer_1_out1 : 16'bz;  // Controlled_Buffer controlled_buffer_2
  and and_1 (and_1_out, rom_1_data[15], rom_1_data[2]);
  Demultiplexer #(.width(16)) demultiplexer_2 (
    .out0(demultiplexer_2_out0), .out1(demultiplexer_2_out1), .in(controlled_buffer_2_out),
    .sel(rom_1_data[2]), .en(rom_1_data[15]));
  Controlled_Buffer #(.width(16)) controlled_buffer_3 (.in(demultiplexer_2_out0), .en(not_2_out));  // open: out
  not not_2 (not_2_out, and_1_out);
  Demultiplexer #(.width(16)) demultiplexer_3 (
    .out0(demultiplexer_3_out0), .out1(demultiplexer_3_out1), .in(controlled_buffer_4_out), .sel(and_2_out),
    .en(and_1_out));
  assign controlled_buffer_4_out = and_1_out ? demultiplexer_2_out1 : 16'bz;  // Controlled_Buffer controlled_buffer_4
  assign {controlled_buffer_5_out_2[15], controlled_buffer_1_out_3, controlled_buffer_5_out, controlled_buffer_5_out_2[2:0]} = not_3_out ? demultiplexer_3_out0 : 16'bz;  // Controlled_Buffer controlled_buffer_5
  not not_3 (not_3_out, and_2_out);
  assign {controlled_buffer_6_out[15], controlled_buffer_5_out, controlled_buffer_6_out_2, controlled_buffer_6_out[2:0]} = and_2_out ? demultiplexer_3_out1 : 16'bz;  // Controlled_Buffer controlled_buffer_6
  and and_2 (and_2_out, and_1_out, rom_1_data[0]);
  Multiplexer #(.width(4), .enable("false")) multiplexer_1 (
    .in0(controlled_buffer_1_out_2[10:7]), .in1(controlled_buffer_6_out_2), .out(multiplexer_1_out),
    .sel(and_2_out));
  RegisterFile registerfile_1 (
    .WriteAddress(controlled_buffer_1_out_3), .WriteData(multiplexer_3_out),
    .ReadAddress_2(controlled_buffer_1_out_2[6:3]), .ReadAddress_1(multiplexer_1_out),
    .ReadData_1(registerfile_1_readdata_1), .ReadData_2(registerfile_1_readdata_2),
    .EnableWrite(multiplexer_2_out), .Clock(clock_1_out), .ClearALL(in_1));
  not not_4 (not_4_out, controlled_buffer_5_out_2[0]);
  not not_5 (not_5_out, controlled_buffer_1_out_2[15]);
  or or_1 (or_1_out, controlled_buffer_6_out[0], not_4_out);
  Multiplexer #(.enable("false")) multiplexer_2 (
    .in0(not_5_out), .in1(or_1_out), .out(multiplexer_2_out), .sel(and_1_out));
  and and_3 (and_3_out, and_1_out, clock_1_out);
  RAM #(.dataWidth(16), .bus("separate")) ram_1 (
    .addr(controlled_buffer_5_out), .din(registerfile_1_readdata_1), .data(ram_1_data),
    .str(controlled_buffer_6_out[0]), .sel(and_1_out), .clk(and_3_out), .ld(controlled_buffer_5_out_2[0]));  // open: clr
  Multiplexer #(.width(16), .enable("false")) multiplexer_3 (
    .in0(alu_1_output), .in1(ram_1_data), .out(multiplexer_3_out), .sel(and_1_out));
  ALU alu_1 (
    .SpecificOp(controlled_buffer_1_out), .in_3(registerfile_1_readdata_1), .in_4(registerfile_1_readdata_2),
    .OUTPUT(alu_1_output), .A_L(controlled_buffer_1_out_2[2]));  // open: FLAG

  // Notes on the sheet:
  //   contents of rom_1 (hex, n*v repeats v):
  //   90 8085 c004
  //   0:ALU, 1:REST
  //   0:branch, 1:memory
  //   0:load, 1:store
endmodule

module ALU (
  input  A_L,
  input  [1:0] SpecificOp,
  input  [15:0] in_3,
  input  [15:0] in_4,
  output FLAG,
  output [15:0] OUTPUT
);

  wire adder_1_cout, and_2_out, subtractor_1_bout;
  wire [15:0] adder_1_out, and_1_out, divider_1_out, divider_1_rem, multiplexer_1_out, multiplexer_2_out,
       multiplier_1_cout, multiplier_1_out, negator_1_out, or_1_out, subtractor_1_out, xor_1_out;

  Adder #(.width(16)) adder_1 (.a(in_3), .b(in_4), .out(adder_1_out), .cout(adder_1_cout));  // open: cin
  Subtractor #(.width(16)) subtractor_1 (
    .a(in_3), .b(in_4), .out(subtractor_1_out), .bout(subtractor_1_bout));  // open: bin
  Multiplier #(.width(16)) multiplier_1 (
    .a(in_3), .b(in_4), .out(multiplier_1_out), .cout(multiplier_1_cout));  // open: cin
  Divider #(.width(16)) divider_1 (.a(in_3), .b(in_4), .out(divider_1_out), .rem(divider_1_rem));  // open: upper
  assign and_1_out = in_3 & in_4;  // AND_Gate and_1, 16 bits wide
  assign or_1_out = in_3 | in_4;  // OR_Gate or_1, 16 bits wide
  assign xor_1_out = in_3 ^ in_4;  // XOR_Gate xor_1, 16 bits wide
  Negator #(.width(16)) negator_1 (.in(in_3), .out(negator_1_out));
  Multiplexer #(.select(2), .width(16), .enable("false")) multiplexer_1 (
    .in0(adder_1_out), .in1(subtractor_1_out), .in2(multiplier_1_out), .in3(divider_1_out),
    .out(multiplexer_1_out), .sel(SpecificOp));
  Multiplexer #(.select(2), .width(16), .enable("false")) multiplexer_2 (
    .in0(and_1_out), .in1(or_1_out), .in2(xor_1_out), .in3(negator_1_out), .out(multiplexer_2_out),
    .sel(SpecificOp));
  Multiplexer #(.width(16), .enable("false")) multiplexer_3 (
    .in0(multiplexer_1_out), .in1(multiplexer_2_out), .out(OUTPUT), .sel(A_L));
  and and_2 (and_2_out, multiplier_1_cout[0], multiplier_1_cout[1], multiplier_1_cout[2], multiplier_1_cout[3], multiplier_1_cout[4], multiplier_1_cout[5], multiplier_1_cout[6], multiplier_1_cout[7], multiplier_1_cout[8], multiplier_1_cout[9], multiplier_1_cout[10], multiplier_1_cout[11], multiplier_1_cout[12], multiplier_1_cout[13], multiplier_1_cout[14], multiplier_1_cout[15], divider_1_rem[0], divider_1_rem[1], divider_1_rem[2], divider_1_rem[3], divider_1_rem[4], divider_1_rem[5], divider_1_rem[6], divider_1_rem[7], divider_1_rem[8], divider_1_rem[9], divider_1_rem[10], divider_1_rem[11], divider_1_rem[12], divider_1_rem[13], divider_1_rem[14], divider_1_rem[15]);
  nor nor_1 (FLAG, adder_1_cout, subtractor_1_bout, and_2_out);

  // Notes on the sheet:
  //   A
  //   TR
  //   ADDER
  //   DIVIDER
  //   AND
  //   OR
  //   XOR
  //   SUBTRACTOR 
  //   MULTIPLIER
  //   NEGATION
endmodule

module RegisterFile (
  input  [3:0] WriteAddress,
  input  [15:0] WriteData,
  input  [3:0] ReadAddress_2,
  input  [3:0] ReadAddress_1,
  input  EnableWrite,
  input  Clock,
  input  ClearALL,
  output [15:0] ReadData_1,
  output [15:0] ReadData_2
);

  wire and_1_out, and_2_out, and_3_out, and_4_out, and_5_out, and_6_out, and_7_out, and_8_out, and_9_out,
       and_10_out, and_11_out, and_12_out, and_13_out, and_14_out, and_15_out, and_16_out, decoder_1_out0,
       decoder_1_out1, decoder_1_out2, decoder_1_out3, decoder_1_out4, decoder_1_out5, decoder_1_out6,
       decoder_1_out7, decoder_1_out8, decoder_1_out9, decoder_1_out10, decoder_1_out11, decoder_1_out12,
       decoder_1_out13, decoder_1_out14, decoder_1_out15;
  wire [15:0] register_1_q, register_2_q, register_3_q, register_4_q, register_5_q, register_6_q,
       register_7_q, register_8_q, register_9_q, register_10_q, register_11_q, register_12_q, register_13_q,
       register_14_q, register_15_q, register_16_q;

  Decoder #(.select(4)) decoder_1 (
    .out0(decoder_1_out0), .out1(decoder_1_out1), .out2(decoder_1_out2), .out3(decoder_1_out3),
    .out4(decoder_1_out4), .out5(decoder_1_out5), .out6(decoder_1_out6), .out7(decoder_1_out7),
    .out8(decoder_1_out8), .out9(decoder_1_out9), .out10(decoder_1_out10), .out11(decoder_1_out11),
    .out12(decoder_1_out12), .out13(decoder_1_out13), .out14(decoder_1_out14), .out15(decoder_1_out15),
    .sel(WriteAddress));  // open: en
  and and_1 (and_1_out, decoder_1_out0, EnableWrite);
  and and_2 (and_2_out, decoder_1_out1, EnableWrite);
  and and_3 (and_3_out, decoder_1_out2, EnableWrite);
  and and_4 (and_4_out, decoder_1_out3, EnableWrite);
  and and_5 (and_5_out, decoder_1_out4, EnableWrite);
  and and_6 (and_6_out, decoder_1_out5, EnableWrite);
  and and_7 (and_7_out, decoder_1_out6, EnableWrite);
  and and_8 (and_8_out, decoder_1_out7, EnableWrite);
  Register #(.width(16)) register_1 (.D(WriteData), .en(and_1_out), .Q(register_1_q), .clk(Clock), .clr(ClearALL));
  Register #(.width(16)) register_2 (.D(WriteData), .en(and_2_out), .Q(register_2_q), .clk(Clock), .clr(ClearALL));
  Register #(.width(16)) register_3 (.D(WriteData), .en(and_3_out), .Q(register_3_q), .clk(Clock), .clr(ClearALL));
  Register #(.width(16)) register_4 (.D(WriteData), .en(and_4_out), .Q(register_4_q), .clk(Clock), .clr(ClearALL));
  Register #(.width(16)) register_5 (.D(WriteData), .en(and_5_out), .Q(register_5_q), .clk(Clock), .clr(ClearALL));
  Register #(.width(16)) register_6 (.D(WriteData), .en(and_6_out), .Q(register_6_q), .clk(Clock), .clr(ClearALL));
  Register #(.width(16)) register_7 (.D(WriteData), .en(and_7_out), .Q(register_7_q), .clk(Clock), .clr(ClearALL));
  Register #(.width(16)) register_8 (.D(WriteData), .en(and_8_out), .Q(register_8_q), .clk(Clock), .clr(ClearALL));
  and and_9 (and_9_out, decoder_1_out8, EnableWrite);
  and and_10 (and_10_out, decoder_1_out9, EnableWrite);
  and and_11 (and_11_out, decoder_1_out10, EnableWrite);
  and and_12 (and_12_out, decoder_1_out11, EnableWrite);
  and and_13 (and_13_out, decoder_1_out12, EnableWrite);
  and and_14 (and_14_out, decoder_1_out13, EnableWrite);
  and and_15 (and_15_out, decoder_1_out14, EnableWrite);
  and and_16 (and_16_out, decoder_1_out15, EnableWrite);
  Register #(.width(16)) register_9 (.D(WriteData), .en(and_9_out), .Q(register_9_q), .clk(Clock), .clr(ClearALL));
  Register #(.width(16)) register_10 (.D(WriteData), .en(and_10_out), .Q(register_10_q), .clk(Clock), .clr(ClearALL));
  Register #(.width(16)) register_11 (.D(WriteData), .en(and_11_out), .Q(register_11_q), .clk(Clock), .clr(ClearALL));
  Register #(.width(16)) register_12 (.D(WriteData), .en(and_12_out), .Q(register_12_q), .clk(Clock), .clr(ClearALL));
  Register #(.width(16)) register_13 (.D(WriteData), .en(and_13_out), .Q(register_13_q), .clk(Clock), .clr(ClearALL));
  Register #(.width(16)) register_14 (.D(WriteData), .en(and_14_out), .Q(register_14_q), .clk(Clock), .clr(ClearALL));
  Register #(.width(16)) register_15 (.D(WriteData), .en(and_15_out), .Q(register_15_q), .clk(Clock), .clr(ClearALL));
  Register #(.width(16)) register_16 (.D(WriteData), .en(and_16_out), .Q(register_16_q), .clk(Clock), .clr(ClearALL));
  Multiplexer #(.select(4), .width(16)) multiplexer_1 (
    .in0(register_1_q), .in1(register_2_q), .in2(register_3_q), .in3(register_4_q), .in4(register_5_q),
    .in5(register_6_q), .in6(register_7_q), .in7(register_8_q), .in8(register_9_q), .in9(register_10_q),
    .in10(register_11_q), .in11(register_12_q), .in12(register_13_q), .in13(register_14_q),
    .in14(register_15_q), .in15(register_16_q), .out(ReadData_1), .sel(ReadAddress_1));  // open: en
  Multiplexer #(.select(4), .width(16)) multiplexer_2 (
    .in0(register_1_q), .in1(register_2_q), .in2(register_3_q), .in3(register_4_q), .in4(register_5_q),
    .in5(register_6_q), .in6(register_7_q), .in7(register_8_q), .in8(register_9_q), .in9(register_10_q),
    .in10(register_11_q), .in11(register_12_q), .in12(register_13_q), .in13(register_14_q),
    .in14(register_15_q), .in15(register_16_q), .out(ReadData_2), .sel(ReadAddress_2));  // open: en
endmodule
